# Fritzing sketch voltmetro&ohmetro (saved by Fritzing 0.9.3b)
stripboards: 1

parts:
  LCD1 = LCD screen
  A1 = arduino-UNO-R4-wifi_1
  R1 = Resistor [tolerance=±5% resistance=2.2 package=THT]
  R2 = Resistor [tolerance=±5% resistance=10k package=THT]
  R3 = Resistor [tolerance=±5% resistance=1k package=THT]
  J1 = shrouded pin header, 10 pins [form="♂ (shrouded male)"]
  J2 = shrouded pin header, 10 pins [form="♂ (shrouded male)"]
  R4 = Trimmer Potentiometer [maximum_resistance=10kΩ package=THT]
  R5 = Resistor [tolerance=±5% resistance=220 package=THT]

nets:
  N1: LCD1.VSS, J2.pin3, J2.pin8
  N2: LCD1.VDD, J1.pin2, J1.pin9, R5.Pin_1
  N3: LCD1.RS, A1.connector45
  N4: LCD1.R/W, LCD1.LED-, J2.pin4, J2.pin7
  N5: LCD1.E, A1.connector44
  N6: LCD1.DB4, A1.connector38
  N7: LCD1.DB5, A1.connector37
  N8: LCD1.DB6, A1.connector36
  N9: LCD1.DB7, A1.connector35
  N10: LCD1.LED+, R5.Pin_0
  N11: A1.connector7, J1.pin3, J1.pin8
  N12: A1.connector9, A1.connector12, R1.Pin_1, J2.pin1, J2.pin10
  N13: A1.connector11, R3.Pin_0
  N14: R1.Pin_0, R2.Pin_1, J2.pin2, J2.pin9, R4.leg2
  N15: J1.pin1, J1.pin10, R4.leg1
  N16: J1.pin4, J1.pin7
  N17: J1.pin5, J1.pin6
  N18: J2.pin5, J2.pin6

notes:
  CAVI DI COLORE:
  VERDE = PIN ANALOGICI
  GIALLI = PIN DIGITALI
  NERO = MASSA
  ROSSO = 5V
  PUNTALI
  VOLTMETRO
  PUNTALI
  OHMETRO
