# Fritzing sketch PROGETTO_VOLTMETRO_ARDUINO (saved by Fritzing 0.9.3b)
perfboards: 1

parts:
  LCD1 = LCD screen
  Componente1 = Arduino Nano (Rev3.0) (ICSP)
  R3 = Trimmer Potentiometer [maximum_resistance=10kΩ package=THT]
  R4 = Resistor [tolerance=±5% resistance=10k package="1206 [SMD]"]  # not connected
  R5 = Resistor [tolerance=±5% resistance=2.2k package="1206 [SMD]"]
  R6 = Resistor [tolerance=±5% resistance=220 package="1206 [SMD]"]
  VCC1 = Battery block 9V  # not connected

nets:
  VSS: LCD1.VSS, LCD1.R/W, Componente1.GND, R3.leg2, R5.Pin_1, R6.Pin_1
  VDD: LCD1.VDD, LCD1.LED+, Componente1.5V, R3.leg1
  N1: LCD1.V0, R3.wiper
  N2: LCD1.RS, Componente1.D12/MISO
  N3: LCD1.E, Componente1.D11/MOSI
  N4: LCD1.DB4, Componente1.D5
  N5: LCD1.DB5, Componente1.D4
  N6: LCD1.DB6, Componente1.D3
  N7: LCD1.DB7, Componente1.D2
  N8: LCD1.LED-, R6.Pin_0
  N9: Componente1.A4, R5.Pin_0

// code stored in the sketch: CODICE_VOLTMETRO_ARDUINO.ino
// BY IGNAZIO SPERANDEO
#include <LiquidCrystal.h>
#define VOLT_ARD 5.0
#define R1 10000.0
#define R2 2000.0

const float inverse = (R1+R2)/R2;
float analog_value;

void setup(){
		lcd.begin(16, 2);
		lcd.print("VOLTMETRO");
}
void loop(){
	analog_value = analogRead(A4);
	float vout = ((analog_value*VOLT_ARD)/1023.0) *	inverse;
	
	lcd.setCursor(0, 1);
	lcd.print(vout);
	lcd.print("V");

	delya(200);

}
